# Fritzing sketch robobatteur (saved by Fritzing 0.9.9b)
breadboards: 2

parts:
  Power_plug1 = Power plug  # not connected
  Composant1 = Arduino Uno (Rev3)
  U2 = OPTO_DARL_6N138S [package=8-smd]
  R4 = Resistor [tolerance=±5% power=0.25 resistance=220 package=THT]
  DIN2 = DIN-5 jack (MIDI) [package=THT]
  R6 = Resistor [tolerance=±5% power=0.25 resistance=220 package=THT]
  D2 = Rectifier Diode [part_number=1N4001 package="300 mil [THT]"]
  R7 = Resistor [tolerance=±5% power=0.25 resistance=4.7k package=THT]

nets:
  N1: Composant1.D0/RX, U2.VOUT, R4.Pin_1
  5V: Composant1.5V, U2.VCC, R4.Pin_0
  GND: Composant1.GND, U2.GND, R7.Pin_1
  N2: U2.A, DIN2.5, R6.Pin_0, D2.cathode
  N3: U2.C, D2.anode
  N4: DIN2.4, R6.Pin_1
